// Logisim project Atividades de exercicio.circ as structural Verilog
module atv1 (
  input  in_1,
  input  A,
  input  in_3,
  input  B,
  input  C,
  input  in_6,
  input  A_2,
  input  X,
  input  B_2,
  input  Y,
  input  C_2,
  input  W,
  input  D,
  input  A_3,
  input  A_4,
  input  B_3,
  input  B_4,
  output out_18,
  output out_19,
  output out_20,
  output out_21,
  output Xor,
  output Xor_2,
  output out_24
);

  wire and_1_out, and_2_out, and_3_out, and_4_out, and_6_out, and_7_out, and_8_out, and_10_out, and_11_out,
       not_1_out, not_2_out, not_3_out, not_4_out, not_5_out, not_6_out, not_7_out, not_8_out, not_9_out,
       not_10_out, or_1_out, or_2_out, or_5_out;

  not not_1 (not_1_out, in_3);
  or or_1 (or_1_out, in_1, in_3);
  or or_2 (or_2_out, not_1_out, in_6);
  not not_2 (not_2_out, C_2);
  and and_1 (and_1_out, C_2, D);
  not not_3 (not_3_out, A_4);
  not not_4 (not_4_out, B_4);
  and and_2 (and_2_out, A_2, B_2);
  not not_5 (not_5_out, and_1_out);
  and and_3 (and_3_out, not_3_out, B_4);
  and and_4 (and_4_out, A_4, not_4_out);
  and and_5 (out_18, or_1_out, or_2_out);
  or or_3 (out_21, and_2_out, not_2_out, not_5_out);
  or or_4 (Xor_2, and_3_out, and_4_out);
  not not_6 (not_6_out, Y);
  not not_7 (not_7_out, A);
  or or_5 (or_5_out, not_6_out, W);
  and and_6 (and_6_out, A, C);
  and and_7 (and_7_out, not_7_out, B, C);
  not not_8 (not_8_out, and_8_out);
  and and_8 (and_8_out, B, C);
  and and_9 (out_20, X, or_5_out);
  not not_9 (not_9_out, A_3);
  not not_10 (not_10_out, B_3);
  or or_6 (out_19, and_6_out, and_7_out, not_8_out);
  and and_10 (and_10_out, not_9_out, B_3);
  or or_7 (Xor, and_10_out, and_11_out);
  and and_11 (and_11_out, A_3, not_10_out);
  and and_12 (out_24, A_3, B_3);

  // Notes on the sheet:
  //   Atividade 1
  //   Atividade 3
  //   Atividade 5
  //   a saída será 1 somente se A e B forem diferentes.
  //   Esse circuito realiza função XOR (Ou exclusivo), mas sem usar essa porta diretamente 
  //   Atividade 2
  //   Atividade 4
  //   Atividade 6
endmodule
